# Fritzing sketch schematic (saved by Fritzing 0.9.5d)
breadboards: 1

parts:
  U1 = lolin
  PWM1 = PCA9685 16x12-bit PWM Breakout
  Bauteil1 = ws2812b [package="smd 2812b"]
  BAT1 = Battery Holders [package=lipo-1100mAh]

nets (from the breadboard view):
  N1: U1.connector0, PWM1.no_name_yet#505, PWM1.no_name_yet#605
  N2: U1.connector26, Bauteil1.VDD
  N3: U1.connector32, PWM1.no_name_yet#504, PWM1.no_name_yet#604
  N4: U1.connector33, PWM1.no_name_yet#503, PWM1.no_name_yet#603
  N5: U1.connector37, PWM1.no_name_yet#501, PWM1.no_name_yet#601, BAT1.-
  N6: PWM1.no_name_yet#506, BAT1.+
